# Fritzing sketch Untitled Sketch 2 (saved by Fritzing 0.9.2b)
circuit board: 8.46667cm x 5.64444cm
breadboards: 1

parts:
  Part1 = Arduino Nano (Rev3.0)
  J1 = Basic Servo
  VCC1 = Battery  # not connected
  VCC2 = Battery  # not connected
  VCC3 = Battery
  VCC4 = Battery  # not connected
  Q1 = PNP-Transistor [package="TO92 [THT]"]
  R1 = Resistor [tolerance=±5% resistance=220 package=THT]
  R2 = Resistor [tolerance=±5% resistance=220 package=THT]
  R3 = Photocell (LDR) [package=THT]
  R4 = Photocell (LDR) [package=THT]
  S1 = Toggle Switch [package=THT]

nets:
  GND: Part1.GND, J1.gnd, VCC3.-, R1.Pin_1, R2.Pin_0
  N1: Part1.D4, S1.L2
  N2: Part1.D5, Q1.E
  N3: Part1.D7, S1.L1
  N4: Part1.D9, J1.pulse
  N5: Part1.VIN, VCC3.+, Q1.B
  5V: Part1.5V, J1.vcc, R3.pin_1, R4.pin_0, S1.COM
  N6: Part1.A1, R2.Pin_1, R3.pin_0
  N7: Part1.A0, R1.Pin_0, R4.pin_1
